// Digital circuit Full_adder_1.dig as structural Verilog
module Full_adder_1 (
  input  B,
  input  A,
  input  Cin,
  output Cout,
  output So
);

  wire and_1_out, and_2_out, or_2_out;

  or or_1 (Cout, and_1_out, and_2_out);
  and and_1 (and_1_out, Cin, or_2_out);
  and and_2 (and_2_out, B, A);
  or or_2 (or_2_out, B, A);
  xor xor_1 (So, B, Cin, A);
endmodule
