// Digital circuit ULA_Complete.dig as structural Verilog
module ULA_Complete (
  input  [15:0] B,
  input  [15:0] A,
  input  [2:0] FUNC,
  output [15:0] R,
  output Zero
);

  wire [15:0] and_gate_1_r, full_adder_complete_1_r, full_adder_complete_2_r, not_1_out, not_gate_1_r,
       or_gate_1_r, shifter_left_1_r, shifter_right_1_r;

  assign not_1_out = ~B;  // Not not_1, 16 bits wide
  Full_Adder_Complete full_adder_complete_1 (.A(A), .B(B), .Cin(1'b0), .R(full_adder_complete_1_r));
  Full_Adder_Complete full_adder_complete_2 (.A(A), .B(not_1_out), .Cin(1'b1), .R(full_adder_complete_2_r));
  And_Gate and_gate_1 (.A(A), .B(B), .R(and_gate_1_r));
  Or_Gate or_gate_1 (.A(A), .B(B), .R(or_gate_1_r));
  Not_Gate not_gate_1 (.A(A), .R(not_gate_1_r));
  Shifter_Left shifter_left_1 (.A(A), .B(B), .R(shifter_left_1_r));
  Shifter_Right shifter_right_1 (.A(A), .B(B), .R(shifter_right_1_r));
  Multiplexer #(.Selector_Bits(3), .Bits(16)) multiplexer_1 (
    .sel(FUNC), .in_0(full_adder_complete_1_r), .in_1(full_adder_complete_2_r), .in_2(and_gate_1_r),
    .in_3(or_gate_1_r), .in_4(not_gate_1_r), .in_5(shifter_left_1_r), .in_6(shifter_right_1_r),
    .in_7({16{1'b0}}), .out(R));
  Zero_Output zero_output_1 (.R(R), .Zero(Zero));
endmodule
