// Digital circuit ControlUnit.dig as structural Verilog
module ControlUnit (
  input  [6:0] OpCode,
  input  Zero,
  input  [2:0] func3,
  input  [6:0] func7,
  output ALUsrc,
  output [2:0] AluOp,
  output [1:0] PcSrc,
  output [1:0] ResultSrc,
  output [2:0] ImmSrc,
  output RegWrite,
  output MemWrite
);

  wire _0, _1, _5, and_1_out, multiplexer_1_out, not_1_out;
  wire [2:0] JALR_d, LOAD_WORD_d, rom_1_d, ULA_CONTROL_B_d, ULA_CONTROL_I_d, ULA_CONTROL_R_d, ULA_CONTROL_S_d;

  not not_1 (not_1_out, Zero);
  Multiplexer multiplexer_1 (.sel(func3[0]), .in_0(Zero), .in_1(not_1_out), .out(multiplexer_1_out));
  ROM #(.AddrBits(7), .Bits(12)) CONTROL (
    .A(OpCode), .sel(1'b1), .D({ImmSrc, ResultSrc, PcSrc[1], _5, ALUsrc, RegWrite, MemWrite, _1, _0}));
  ROM #(.AddrBits(4), .Bits(3)) ULA_CONTROL_R (.A({func7[5], func3}), .sel(1'b1), .D(ULA_CONTROL_R_d));
  ROM #(.Bits(3)) ULA_CONTROL_I (.A(func3[1:0]), .sel(1'b1), .D(ULA_CONTROL_I_d));
  ROM #(.Bits(3)) LOAD_WORD (.A(func3[1:0]), .sel(1'b1), .D(LOAD_WORD_d));
  ROM #(.Bits(3)) ULA_CONTROL_S (.A(func3[1:0]), .sel(1'b1), .D(ULA_CONTROL_S_d));
  ROM #(.Bits(3)) ULA_CONTROL_B (.A(func3[1:0]), .sel(1'b1), .D(ULA_CONTROL_B_d));
  ROM #(.Bits(3)) JALR (.A(func3[1:0]), .sel(1'b1), .D(JALR_d));
  ROM #(.AddrBits(7), .Bits(3)) rom_1 (.A(OpCode), .sel(1'b1), .D(rom_1_d));
  and and_1 (and_1_out, multiplexer_1_out, _0);
  or or_1 (PcSrc[0], and_1_out, _1);
  Multiplexer #(.Selector_Bits(3), .Bits(3)) multiplexer_2 (
    .sel(rom_1_d), .in_0(ULA_CONTROL_R_d), .in_1(ULA_CONTROL_I_d), .in_2(LOAD_WORD_d),
    .in_3(ULA_CONTROL_S_d), .in_4(ULA_CONTROL_B_d), .in_5(JALR_d), .in_6(3'b000), .in_7(3'b000), .out(AluOp));

  // Other names for the same wires on the sheet: _2 = MemWrite; _3 = RegWrite; _4 = ALUsrc; _6 = PcSrc[1];
  //   _7 = ResultSrc[0]; _8 = ResultSrc[1]; _9 = ImmSrc[0]; _10 = ImmSrc[1]; _11 = ImmSrc[2]; f3[2:0] = func3;
  //   f7[6:0] = func7

  // Notes on the sheet:
  //   contents of CONTROL (hex, n*v repeats v):
  //   0,0,0,118,15*0,18,15*0,214,15*0,8,0,0,0,688,43*0,421,0,0,0,1fa
  //   ,7*0,9ba,0,0,0,40
  //   contents of ULA_CONTROL_R (hex, n*v repeats v):
  //   0,3,2,0,4,0,5,7,1,247*0,1
  //   contents of ULA_CONTROL_I (hex, n*v repeats v):
  //   0,0,2
  //   contents of ULA_CONTROL_B (hex, n*v repeats v):
  //   1,1
  //   contents of rom_1 (hex, n*v repeats v):
  //   0,0,0,2,15*0,1,15*0,3,63*0,4,0,0,0,5
endmodule
