// Digital circuit mainCpu.dig as structural Verilog
module mainCpu (
  input  clk,
  output [31:0] out_2,
  output [6:0] out_3,
  output [4:0] out_4,
  output [4:0] out_5,
  output [31:0] out_6,
  output [31:0] out_7,
  output [31:0] out_8,
  output [31:0] out_9,
  output [31:0] out_10,
  output [31:0] out_11,
  output [31:0] out_12,
  output [31:0] out_13,
  output [31:0] out_14,
  output [31:0] out_15
);

  wire ALUSrc, MemWRITE, not_1_out, RegWrite, zero;
  wire [1:0] PcSrc, ResultSrc;
  wire [2:0] ALUop, f3, ImmSrc;
  wire [6:0] f7;
  wire [11:7] Instruction;
  wire [31:0] HALT_s, JALR, multiplexer_1_out, multiplexer_2_out, PC_plus_4, ramdualport_1_d, RS1_out,
       RS2_out;

  Add #(.Bits(32)) PC__plus__4 (.a(out_7), .b(32'h4), .c_i(1'b0), .s(PC_plus_4));  // open: c_o
  Add #(.Bits(32)) PC__plus__IMM (.a(out_7), .b(out_2), .c_i(1'b0), .s(out_9));  // open: c_o
  Add #(.Bits(32)) HALT (.a(out_7), .b({32{1'b0}}), .c_i(1'b0), .s(HALT_s));  // open: c_o
  Multiplexer #(.Selector_Bits(2), .Bits(32)) multiplexer_1 (
    .sel(PcSrc), .in_0(PC_plus_4), .in_1(out_9), .in_2(HALT_s), .in_3(JALR), .out(multiplexer_1_out));
  D_FF #(.Bits(32)) PC (.D(multiplexer_1_out), .C(clk), .Q(out_7));  // open: nQ
  ROM #(.AddrBits(16), .Bits(32)) text (.A(out_7[15:0]), .sel(1'b1), .D({f7, out_4, out_5, f3, Instruction, out_3}));
  immediateGenerate immediategenerate_1 (
    .ImmSel(ImmSrc), .instruction({f7, out_4, out_5, f3, Instruction, out_3}), .out(out_2));
  ControlUnit controlunit_1 (
    .OpCode(out_3), .Zero(zero), .func3(f3), .func7(f7), .MemWrite(MemWRITE), .RegWrite(RegWrite),
    .ALUsrc(ALUSrc), .PcSrc(PcSrc), .ResultSrc(ResultSrc), .ImmSrc(ImmSrc), .AluOp(ALUop));
  registerFile registerfile_1 (
    .rsi1(out_5), .rsi2(out_4), .rdi(Instruction), .data(out_6), .WE(RegWrite), .clk(clk), .rs1(RS1_out),
    .rs2(RS2_out), .x5Data(out_8), .x6Data(out_10), .x9Data(out_11), .x8Data(out_13), .x7Data(out_12),
    .x2Data(out_14), .x1Data(out_15));
  Multiplexer #(.Bits(32)) multiplexer_2 (.sel(ALUSrc), .in_0(RS2_out), .in_1(out_2), .out(multiplexer_2_out));
  ALU alu_1 (.SrcA(RS1_out), .SrcB(multiplexer_2_out), .ALUOp(ALUop), .R(JALR), .Zero(zero));
  not not_1 (not_1_out, MemWRITE);
  RAMDualPort #(.AddrBits(24), .Bits(32)) ramdualport_1 (
    .A(JALR[23:0]), .Din(RS2_out), .str(MemWRITE), .C(clk), .ld(not_1_out), .D(ramdualport_1_d));
  Multiplexer #(.Selector_Bits(2), .Bits(32)) multiplexer_3 (
    .sel(ResultSrc), .in_0(JALR), .in_1(out_2), .in_2(ramdualport_1_d), .in_3(PC_plus_4), .out(out_6));

  // Other names for the same wires on the sheet: DATAX1[31:0] = out_15; DATAX2[31:0] = out_14; DATAX5[31:0] = out_8;
  //   DATAX6[31:0] = out_10; DATAX7[31:0] = out_12; DATAX8[31:0] = out_13; DATAX9[31:0] = out_11;
  //   ImmOut[31:0] = out_2; Instruction (some bits) = {f7, out_4, out_5, f3, out_3}; OPCODE[6:0] = out_3;
  //   RD[4:0] = Instruction; RS1[4:0] = out_5; RS2[4:0] = out_4; pc__plus__imm[31:0] = out_9; PcAddr[31:0] = out_7;
  //   Result[31:0] = out_6; ULA_result[31:0] = JALR

  // Notes on the sheet:
  //   Debug
  //   contents of text (hex, n*v repeats v):
  //   800293,0,0,0,200313,0,0,0,332413,0,0,0,232413,0,0,0,132413,0,0,0
  //   ,62a433,0,0,0,532433,0,0,0,632433,0,0,0,6283b3,0,0,0,406282b3
  //   ,0,0,0,62c433,0,0,0,62e433,0,0,0,62f433,0,0,0,629433,0,0,0,40000113
  //   ,0,0,0,512023,0,0,0,612223,0,0,0,12303,0,0,0,412283,0,0,0,ff4b7
  //   ,0,0,0,863,0,0,0,628c63,0,0,0,529a63,0,0,0,629663,0,0,0,ff5ff0ef
  //   ,0,0,0,100073,0,0,0,8067,0,0,0,100293,0,0,0,100073,0,0,0,a
endmodule
