// Digital circuit ALU.dig as structural Verilog
module ALU (
  input  [31:0] SrcA,
  input  [31:0] SrcB,
  input  [2:0] ALUOp,
  output [31:0] R,
  output Zero
);

  wire [0:0] comparator_1_lt;
  wire [31:0] add_1_s, and_1_out, barrelshifter_1_out, or_1_out, sub_1_s, xor_1_out;

  Comparator #(.Bits(32)) comparator_1 (.a(SrcA), .b(SrcB), .lt(comparator_1_lt[0]));  // open: gt, eq
  assign xor_1_out = SrcA ^ SrcB;  // XOr xor_1, 32 bits wide
  assign or_1_out = SrcA | SrcB;  // Or or_1, 32 bits wide
  assign and_1_out = SrcA & SrcB;  // And and_1, 32 bits wide
  Add #(.Bits(32)) add_1 (.a(SrcA), .b(SrcB), .c_i(1'b0), .s(add_1_s));  // open: c_o
  Sub #(.Bits(32)) sub_1 (.a(SrcA), .b(SrcB), .c_i(1'b0), .s(sub_1_s));  // open: c_o
  BarrelShifter #(.Bits(32)) barrelshifter_1 (.in(SrcA), .shift(SrcB[5:0]), .out(barrelshifter_1_out));
  Multiplexer #(.Selector_Bits(3), .Bits(32)) multiplexer_1 (
    .sel(ALUOp), .in_0(add_1_s), .in_1(sub_1_s), .in_2({{31{1'b0}}, comparator_1_lt[0]}),
    .in_3(barrelshifter_1_out), .in_4(xor_1_out), .in_5(or_1_out), .in_6({32{1'b0}}), .in_7(and_1_out),
    .out(R));
  nor nor_1 (Zero, R[0], R[1], R[2], R[3], R[4], R[5], R[6], R[7], R[8], R[9], R[10], R[11], R[12], R[13], R[14], R[15], R[16], R[17], R[18], R[19], R[20], R[21], R[22], R[23], R[24], R[25], R[26], R[27], R[28], R[29], R[30], R[31]);
endmodule
