// Digital circuit immediateGenerate.dig as structural Verilog
module immediateGenerate (
  input  [2:0] ImmSel,
  input  [31:0] instruction,
  output [31:0] out
);

  wire [31:0] B, I, J, S;

  BitExtender #(.inputBits(13), .outputBits(32)) bitextender_1 (
    .in({instruction[31], instruction[7], instruction[30:25], instruction[11:8], 1'b0}), .out(B));
  Multiplexer #(.Selector_Bits(3), .Bits(32)) multiplexer_1 (
    .sel(ImmSel), .in_0(I), .in_1(S), .in_2(B), .in_3({instruction[31:12], {12{1'b0}}}), .in_4(J),
    .in_5({32{1'b0}}), .in_6({32{1'b0}}), .in_7({32{1'b0}}), .out(out));
  BitExtender #(.inputBits(12), .outputBits(32)) bitextender_2 (.in(instruction[31:20]), .out(I));
  BitExtender #(.inputBits(12), .outputBits(32)) bitextender_3 (.in({instruction[31:25], instruction[11:7]}), .out(S));
  BitExtender #(.inputBits(21), .outputBits(32)) bitextender_4 (
    .in({instruction[31], instruction[19:12], instruction[20], instruction[30:21], 1'b0}), .out(J));

  // Other names for the same wires on the sheet: _7 = instruction[7]; _8 = instruction[8]; _9 = instruction[9];
  //   _10 = instruction[10]; _11 = instruction[11]; _12 = instruction[12]; U[31:12] = instruction[31:12];
  //   _13 = instruction[13]; _14 = instruction[14]; _15 = instruction[15]; _16 = instruction[16];
  //   _17 = instruction[17]; _18 = instruction[18]; _19 = instruction[19]; _20 = instruction[20];
  //   _21 = instruction[21]; _22 = instruction[22]; _23 = instruction[23]; _24 = instruction[24];
  //   _25 = instruction[25]; _26 = instruction[26]; _27 = instruction[27]; _28 = instruction[28];
  //   _29 = instruction[29]; _30 = instruction[30]; _31 = instruction[31]
endmodule
