// Digital circuit registerFile.dig as structural Verilog
module registerFile (
  input  [4:0] rsi1,
  input  [4:0] rsi2,
  input  [4:0] rdi,
  input  [31:0] data,
  input  WE,
  input  clk,
  output [31:0] rs1,
  output [31:0] rs2,
  output [31:0] x5Data,
  output [31:0] x6Data,
  output [31:0] x9Data,
  output [31:0] x8Data,
  output [31:0] x7Data,
  output [31:0] x2Data,
  output [31:0] x1Data
);

  wire x1we, x2we, x3we, x4we, x5we, x6we, x7we, x8we, x9we, x10we, x11we, x12we, x13we, x14we, x15we, x16we,
       x17we, x18we, x19we, x20we, x21we, x22we, x23we, x24we, x25we, x26we, x27we, x28we, x29we, x30we,
       x31we;
  wire [31:0] x3_data, x4_data, x10_data, x11_data, x12_data, x13_data, x14_data, x15_data, x16_data,
       x17_data, x18_data, x19_data, x20_data, x21_data, x22_data, x23_data, x24_data, x25_data, x26_data,
       x27_data, x28_data, x29_data, x30_data, x31_data;

  Demultiplexer #(.Selector_Bits(5)) demultiplexer_1 (
    .sel(rdi), .in(WE), .out_1(x1we), .out_2(x2we), .out_3(x3we), .out_4(x4we), .out_5(x5we), .out_6(x6we),
    .out_7(x7we), .out_8(x8we), .out_9(x9we), .out_10(x10we), .out_11(x11we), .out_12(x12we), .out_13(x13we),
    .out_14(x14we), .out_15(x15we), .out_16(x16we), .out_17(x17we), .out_18(x18we), .out_19(x19we),
    .out_20(x20we), .out_21(x21we), .out_22(x22we), .out_23(x23we), .out_24(x24we), .out_25(x25we),
    .out_26(x26we), .out_27(x27we), .out_28(x28we), .out_29(x29we), .out_30(x30we), .out_31(x31we));  // open: out_0
  Register #(.Bits(32)) x1 (.D(data), .C(clk), .en(x1we), .Q(x1Data));
  Register #(.Bits(32)) x2 (.D(data), .C(clk), .en(x2we), .Q(x2Data));
  Register #(.Bits(32)) x3 (.D(data), .C(clk), .en(x3we), .Q(x3_data));
  Register #(.Bits(32)) x4 (.D(data), .C(clk), .en(x4we), .Q(x4_data));
  Register #(.Bits(32)) x5 (.D(data), .C(clk), .en(x5we), .Q(x5Data));
  Register #(.Bits(32)) x6 (.D(data), .C(clk), .en(x6we), .Q(x6Data));
  Register #(.Bits(32)) x7 (.D(data), .C(clk), .en(x7we), .Q(x7Data));
  Register #(.Bits(32)) x8 (.D(data), .C(clk), .en(x8we), .Q(x8Data));
  Register #(.Bits(32)) x9 (.D(data), .C(clk), .en(x9we), .Q(x9Data));
  Register #(.Bits(32)) x10 (.D(data), .C(clk), .en(x10we), .Q(x10_data));
  Register #(.Bits(32)) x11 (.D(data), .C(clk), .en(x11we), .Q(x11_data));
  Register #(.Bits(32)) x12 (.D(data), .C(clk), .en(x12we), .Q(x12_data));
  Register #(.Bits(32)) x13 (.D(data), .C(clk), .en(x13we), .Q(x13_data));
  Register #(.Bits(32)) x14 (.D(data), .C(clk), .en(x14we), .Q(x14_data));
  Register #(.Bits(32)) x15 (.D(data), .C(clk), .en(x15we), .Q(x15_data));
  Register #(.Bits(32)) x16 (.D(data), .C(clk), .en(x16we), .Q(x16_data));
  Register #(.Bits(32)) x17 (.D(data), .C(clk), .en(x17we), .Q(x17_data));
  Register #(.Bits(32)) x18 (.D(data), .C(clk), .en(x18we), .Q(x18_data));
  Register #(.Bits(32)) x19 (.D(data), .C(clk), .en(x19we), .Q(x19_data));
  Register #(.Bits(32)) x20 (.D(data), .C(clk), .en(x20we), .Q(x20_data));
  Register #(.Bits(32)) x21 (.D(data), .C(clk), .en(x21we), .Q(x21_data));
  Register #(.Bits(32)) x22 (.D(data), .C(clk), .en(x22we), .Q(x22_data));
  Register #(.Bits(32)) x23 (.D(data), .C(clk), .en(x23we), .Q(x23_data));
  Register #(.Bits(32)) x24 (.D(data), .C(clk), .en(x24we), .Q(x24_data));
  Register #(.Bits(32)) x25 (.D(data), .C(clk), .en(x25we), .Q(x25_data));
  Register #(.Bits(32)) x26 (.D(data), .C(clk), .en(x26we), .Q(x26_data));
  Register #(.Bits(32)) x27 (.D(data), .C(clk), .en(x27we), .Q(x27_data));
  Register #(.Bits(32)) x28 (.D(data), .C(clk), .en(x28we), .Q(x28_data));
  Register #(.Bits(32)) x29 (.D(data), .C(clk), .en(x29we), .Q(x29_data));
  Register #(.Bits(32)) x30 (.D(data), .C(clk), .en(x30we), .Q(x30_data));
  Register #(.Bits(32)) x31 (.D(data), .C(clk), .en(x31we), .Q(x31_data));
  Multiplexer #(.Selector_Bits(5), .Bits(32)) multiplexer_1 (
    .sel(rsi1), .in_0({32{1'b0}}), .in_1(x1Data), .in_2(x2Data), .in_3(x3_data), .in_4(x4_data),
    .in_5(x5Data), .in_6(x6Data), .in_7(x7Data), .in_8(x8Data), .in_9(x9Data), .in_10(x10_data),
    .in_11(x11_data), .in_12(x12_data), .in_13(x13_data), .in_14(x14_data), .in_15(x15_data),
    .in_16(x16_data), .in_17(x17_data), .in_18(x18_data), .in_19(x19_data), .in_20(x20_data),
    .in_21(x21_data), .in_22(x22_data), .in_23(x23_data), .in_24(x24_data), .in_25(x25_data),
    .in_26(x26_data), .in_27(x27_data), .in_28(x28_data), .in_29(x29_data), .in_30(x30_data),
    .in_31(x31_data), .out(rs1));
  Multiplexer #(.Selector_Bits(5), .Bits(32)) multiplexer_2 (
    .sel(rsi2), .in_0({32{1'b0}}), .in_1(x1Data), .in_2(x2Data), .in_3(x3_data), .in_4(x4_data),
    .in_5(x5Data), .in_6(x6Data), .in_7(x7Data), .in_8(x8Data), .in_9(x9Data), .in_10(x10_data),
    .in_11(x11_data), .in_12(x12_data), .in_13(x13_data), .in_14(x14_data), .in_15(x15_data),
    .in_16(x16_data), .in_17(x17_data), .in_18(x18_data), .in_19(x19_data), .in_20(x20_data),
    .in_21(x21_data), .in_22(x22_data), .in_23(x23_data), .in_24(x24_data), .in_25(x25_data),
    .in_26(x26_data), .in_27(x27_data), .in_28(x28_data), .in_29(x29_data), .in_30(x30_data),
    .in_31(x31_data), .out(rs2));

  // Other names for the same wires on the sheet: data_t[31:0] = data; rdi_t[4:0] = rdi; rs1_t[31:0] = rs1;
  //   rs2_t[31:0] = rs2; rsi1_t[4:0] = rsi1; rsi2_t[4:0] = rsi2; x1_data[31:0] = x1Data; x2_data[31:0] = x2Data;
  //   x5_data[31:0] = x5Data; x6_data[31:0] = x6Data; x7_data[31:0] = x7Data; x8_data[31:0] = x8Data;
  //   x9_data[31:0] = x9Data

  // Notes on the sheet:
  //   regBankDebug
endmodule
