// Digital circuit SetasDoCarroComJK.dig as structural Verilog
module SetasDoCarroComJK (
  input  clk,
  input  RIGHT,
  input  LEFT,
  input  HAZ,
  output LA,
  output LB,
  output LC,
  output RC,
  output RB,
  output RA
);

  wire and_1_out, and_2_out, and_3_out, and_4_out, and_5_out, and_6_out, decoder_1_out_1, decoder_1_out_2,
       decoder_1_out_3, FF0_2_q, FF0_3_q, FF0_q, FF1_2_q, FF1_q, not_1_out, not_2_out, not_3_out, not_4_out,
       or_1_out, or_2_out, or_3_out, or_4_out;
  wire [1:0] or_11_out;

  Decoder #(.Selector_Bits(2)) decoder_1 (
    .sel(or_11_out), .out_1(decoder_1_out_1), .out_2(decoder_1_out_2), .out_3(decoder_1_out_3));  // open: out_0
  not not_1 (not_1_out, decoder_1_out_1);
  not not_2 (not_2_out, decoder_1_out_2);
  and and_1 (and_1_out, FF0_q, decoder_1_out_1);
  or or_1 (or_1_out, FF0_q, not_1_out);
  and and_2 (and_2_out, decoder_1_out_2, FF0_2_q);
  or or_2 (or_2_out, FF0_2_q, not_2_out);
  JK_FF FF0 (.J(decoder_1_out_1), .C(clk), .K(FF0_q), .Q(FF0_q));  // open: nQ
  JK_FF FF1 (.J(and_1_out), .C(clk), .K(or_1_out), .Q(FF1_q));  // open: nQ
  JK_FF FF0_2 (.J(decoder_1_out_2), .C(clk), .K(FF0_2_q), .Q(FF0_2_q));  // open: nQ
  JK_FF FF1_2 (.J(and_2_out), .C(clk), .K(or_2_out), .Q(FF1_2_q));  // open: nQ
  JK_FF FF0_3 (.J(decoder_1_out_3), .C(clk), .K(1'b1), .Q(FF0_3_q));  // open: nQ
  and and_3 (and_3_out, FF0_q, FF1_q);
  or or_3 (or_3_out, FF0_q, FF1_q);
  or or_4 (or_4_out, FF0_2_q, FF1_2_q);
  and and_4 (and_4_out, FF0_2_q, FF1_2_q);
  or or_5 (RC, and_3_out, FF0_3_q);
  or or_6 (RB, FF1_q, FF0_3_q);
  or or_7 (RA, or_3_out, FF0_3_q);
  or or_8 (LA, or_4_out, FF0_3_q);
  or or_9 (LB, FF1_2_q, FF0_3_q);
  or or_10 (LC, and_4_out, FF0_3_q);
  not not_3 (not_3_out, RIGHT);
  and and_5 (and_5_out, LEFT, not_3_out);
  or or_11 (or_11_out[1], and_5_out, HAZ);
  not not_4 (not_4_out, LEFT);
  and and_6 (and_6_out, RIGHT, not_4_out);
  or or_12 (or_11_out[0], and_6_out, HAZ);
endmodule
