// Digital circuit Full_Adder_Complete.dig as structural Verilog
module Full_Adder_Complete (
  input  [15:0] A,
  input  [15:0] B,
  input  Cin,
  output [15:0] R
);

  wire full_adder_4_2_cout, full_adder_4_3_cout, full_adder_4_4_cout;

  Full_adder_4 full_adder_4_1 (.A(A[15:12]), .B(B[15:12]), .Cin(full_adder_4_2_cout), .S4(R[15:12]));  // open: Cout
  Full_adder_4 full_adder_4_2 (
    .A(A[11:8]), .B(B[11:8]), .Cin(full_adder_4_3_cout), .S4(R[11:8]), .Cout(full_adder_4_2_cout));
  Full_adder_4 full_adder_4_3 (
    .A(A[7:4]), .B(B[7:4]), .Cin(full_adder_4_4_cout), .S4(R[7:4]), .Cout(full_adder_4_3_cout));
  Full_adder_4 full_adder_4_4 (.A(A[3:0]), .B(B[3:0]), .Cin(Cin), .S4(R[3:0]), .Cout(full_adder_4_4_cout));

  // Other names for the same wires on the sheet: A0[3:0] = A[3:0]; A1[3:0] = A[7:4]; A2[3:0] = A[11:8];
  //   A3[3:0] = A[15:12]; B0[3:0] = B[3:0]; B1[3:0] = B[7:4]; B2[3:0] = B[11:8]; B3[3:0] = B[15:12]
endmodule
