// Digital circuit Full_adder_4.dig as structural Verilog
module Full_adder_4 (
  input  [3:0] A,
  input  [3:0] B,
  input  Cin,
  output [3:0] S4,
  output Cout
);

  wire full_adder_1_2_cout, full_adder_1_3_cout, full_adder_1_4_cout;

  Full_adder_1 full_adder_1_1 (.B(B[3]), .A(A[3]), .Cin(full_adder_1_2_cout), .Cout(Cout), .So(S4[3]));
  Full_adder_1 full_adder_1_2 (.B(B[2]), .A(A[2]), .Cin(full_adder_1_3_cout), .Cout(full_adder_1_2_cout), .So(S4[2]));
  Full_adder_1 full_adder_1_3 (.B(B[1]), .A(A[1]), .Cin(full_adder_1_4_cout), .Cout(full_adder_1_3_cout), .So(S4[1]));
  Full_adder_1 full_adder_1_4 (.B(B[0]), .A(A[0]), .Cin(Cin), .Cout(full_adder_1_4_cout), .So(S4[0]));
endmodule
