// Digital circuit Shifter_Right.dig as structural Verilog
module Shifter_Right (
  input  [15:0] A,
  input  [15:0] B,
  output [15:0] R
);

  wire multiplexer_1_out, multiplexer_2_out, multiplexer_3_out, multiplexer_4_out, multiplexer_5_out,
       multiplexer_6_out, multiplexer_7_out, multiplexer_8_out, multiplexer_9_out, multiplexer_10_out,
       multiplexer_11_out, multiplexer_12_out, multiplexer_13_out, multiplexer_14_out, multiplexer_15_out,
       multiplexer_16_out, multiplexer_17_out, multiplexer_18_out, multiplexer_19_out, multiplexer_20_out,
       multiplexer_21_out, multiplexer_22_out, multiplexer_23_out, multiplexer_24_out, multiplexer_25_out,
       multiplexer_26_out, multiplexer_27_out, multiplexer_28_out, multiplexer_29_out, multiplexer_30_out,
       multiplexer_31_out, multiplexer_32_out, multiplexer_33_out, multiplexer_34_out, multiplexer_35_out,
       multiplexer_36_out, multiplexer_37_out, multiplexer_38_out, multiplexer_39_out, multiplexer_40_out,
       multiplexer_41_out, multiplexer_42_out, multiplexer_43_out, multiplexer_44_out, multiplexer_45_out,
       multiplexer_46_out, multiplexer_47_out, multiplexer_48_out;

  Multiplexer multiplexer_1 (.sel(B[0]), .in_0(A[0]), .in_1(A[1]), .out(multiplexer_1_out));
  Multiplexer multiplexer_2 (.sel(B[0]), .in_0(A[1]), .in_1(A[2]), .out(multiplexer_2_out));
  Multiplexer multiplexer_3 (.sel(B[0]), .in_0(A[2]), .in_1(A[3]), .out(multiplexer_3_out));
  Multiplexer multiplexer_4 (.sel(B[0]), .in_0(A[3]), .in_1(A[4]), .out(multiplexer_4_out));
  Multiplexer multiplexer_5 (.sel(B[0]), .in_0(A[4]), .in_1(A[5]), .out(multiplexer_5_out));
  Multiplexer multiplexer_6 (.sel(B[0]), .in_0(A[5]), .in_1(A[6]), .out(multiplexer_6_out));
  Multiplexer multiplexer_7 (.sel(B[0]), .in_0(A[6]), .in_1(A[7]), .out(multiplexer_7_out));
  Multiplexer multiplexer_8 (.sel(B[0]), .in_0(A[7]), .in_1(A[8]), .out(multiplexer_8_out));
  Multiplexer multiplexer_9 (.sel(B[0]), .in_0(A[8]), .in_1(A[9]), .out(multiplexer_9_out));
  Multiplexer multiplexer_10 (.sel(B[0]), .in_0(A[9]), .in_1(A[10]), .out(multiplexer_10_out));
  Multiplexer multiplexer_11 (.sel(B[0]), .in_0(A[10]), .in_1(A[11]), .out(multiplexer_11_out));
  Multiplexer multiplexer_12 (.sel(B[0]), .in_0(A[11]), .in_1(A[12]), .out(multiplexer_12_out));
  Multiplexer multiplexer_13 (.sel(B[0]), .in_0(A[12]), .in_1(A[13]), .out(multiplexer_13_out));
  Multiplexer multiplexer_14 (.sel(B[0]), .in_0(A[13]), .in_1(A[14]), .out(multiplexer_14_out));
  Multiplexer multiplexer_15 (.sel(B[0]), .in_0(A[14]), .in_1(A[15]), .out(multiplexer_15_out));
  Multiplexer multiplexer_16 (.sel(B[0]), .in_0(A[15]), .in_1(1'b0), .out(multiplexer_16_out));
  Multiplexer multiplexer_17 (.sel(B[1]), .in_0(multiplexer_1_out), .in_1(multiplexer_3_out), .out(multiplexer_17_out));
  Multiplexer multiplexer_18 (.sel(B[1]), .in_0(multiplexer_2_out), .in_1(multiplexer_4_out), .out(multiplexer_18_out));
  Multiplexer multiplexer_19 (.sel(B[1]), .in_0(multiplexer_3_out), .in_1(multiplexer_5_out), .out(multiplexer_19_out));
  Multiplexer multiplexer_20 (.sel(B[1]), .in_0(multiplexer_4_out), .in_1(multiplexer_6_out), .out(multiplexer_20_out));
  Multiplexer multiplexer_21 (.sel(B[1]), .in_0(multiplexer_5_out), .in_1(multiplexer_7_out), .out(multiplexer_21_out));
  Multiplexer multiplexer_22 (.sel(B[1]), .in_0(multiplexer_6_out), .in_1(multiplexer_8_out), .out(multiplexer_22_out));
  Multiplexer multiplexer_23 (.sel(B[1]), .in_0(multiplexer_7_out), .in_1(multiplexer_9_out), .out(multiplexer_23_out));
  Multiplexer multiplexer_24 (
    .sel(B[1]), .in_0(multiplexer_8_out), .in_1(multiplexer_10_out), .out(multiplexer_24_out));
  Multiplexer multiplexer_25 (
    .sel(B[1]), .in_0(multiplexer_9_out), .in_1(multiplexer_11_out), .out(multiplexer_25_out));
  Multiplexer multiplexer_26 (
    .sel(B[1]), .in_0(multiplexer_10_out), .in_1(multiplexer_12_out), .out(multiplexer_26_out));
  Multiplexer multiplexer_27 (
    .sel(B[1]), .in_0(multiplexer_11_out), .in_1(multiplexer_13_out), .out(multiplexer_27_out));
  Multiplexer multiplexer_28 (
    .sel(B[1]), .in_0(multiplexer_12_out), .in_1(multiplexer_14_out), .out(multiplexer_28_out));
  Multiplexer multiplexer_29 (
    .sel(B[1]), .in_0(multiplexer_13_out), .in_1(multiplexer_15_out), .out(multiplexer_29_out));
  Multiplexer multiplexer_30 (
    .sel(B[1]), .in_0(multiplexer_14_out), .in_1(multiplexer_16_out), .out(multiplexer_30_out));
  Multiplexer multiplexer_31 (.sel(B[1]), .in_0(multiplexer_15_out), .in_1(1'b0), .out(multiplexer_31_out));
  Multiplexer multiplexer_32 (.sel(B[1]), .in_0(multiplexer_16_out), .in_1(1'b0), .out(multiplexer_32_out));
  Multiplexer multiplexer_33 (
    .sel(B[2]), .in_0(multiplexer_17_out), .in_1(multiplexer_21_out), .out(multiplexer_33_out));
  Multiplexer multiplexer_34 (
    .sel(B[2]), .in_0(multiplexer_18_out), .in_1(multiplexer_22_out), .out(multiplexer_34_out));
  Multiplexer multiplexer_35 (
    .sel(B[2]), .in_0(multiplexer_19_out), .in_1(multiplexer_23_out), .out(multiplexer_35_out));
  Multiplexer multiplexer_36 (
    .sel(B[2]), .in_0(multiplexer_20_out), .in_1(multiplexer_24_out), .out(multiplexer_36_out));
  Multiplexer multiplexer_37 (
    .sel(B[2]), .in_0(multiplexer_21_out), .in_1(multiplexer_25_out), .out(multiplexer_37_out));
  Multiplexer multiplexer_38 (
    .sel(B[2]), .in_0(multiplexer_22_out), .in_1(multiplexer_26_out), .out(multiplexer_38_out));
  Multiplexer multiplexer_39 (
    .sel(B[2]), .in_0(multiplexer_23_out), .in_1(multiplexer_27_out), .out(multiplexer_39_out));
  Multiplexer multiplexer_40 (
    .sel(B[2]), .in_0(multiplexer_24_out), .in_1(multiplexer_28_out), .out(multiplexer_40_out));
  Multiplexer multiplexer_41 (
    .sel(B[2]), .in_0(multiplexer_25_out), .in_1(multiplexer_29_out), .out(multiplexer_41_out));
  Multiplexer multiplexer_42 (
    .sel(B[2]), .in_0(multiplexer_26_out), .in_1(multiplexer_30_out), .out(multiplexer_42_out));
  Multiplexer multiplexer_43 (
    .sel(B[2]), .in_0(multiplexer_27_out), .in_1(multiplexer_31_out), .out(multiplexer_43_out));
  Multiplexer multiplexer_44 (
    .sel(B[2]), .in_0(multiplexer_28_out), .in_1(multiplexer_32_out), .out(multiplexer_44_out));
  Multiplexer multiplexer_45 (.sel(B[2]), .in_0(multiplexer_29_out), .in_1(1'b0), .out(multiplexer_45_out));
  Multiplexer multiplexer_46 (.sel(B[2]), .in_0(multiplexer_30_out), .in_1(1'b0), .out(multiplexer_46_out));
  Multiplexer multiplexer_47 (.sel(B[2]), .in_0(multiplexer_31_out), .in_1(1'b0), .out(multiplexer_47_out));
  Multiplexer multiplexer_48 (.sel(B[2]), .in_0(multiplexer_32_out), .in_1(1'b0), .out(multiplexer_48_out));
  Multiplexer multiplexer_49 (.sel(B[3]), .in_0(multiplexer_33_out), .in_1(multiplexer_41_out), .out(R[0]));
  Multiplexer multiplexer_50 (.sel(B[3]), .in_0(multiplexer_34_out), .in_1(multiplexer_42_out), .out(R[1]));
  Multiplexer multiplexer_51 (.sel(B[3]), .in_0(multiplexer_35_out), .in_1(multiplexer_43_out), .out(R[2]));
  Multiplexer multiplexer_52 (.sel(B[3]), .in_0(multiplexer_36_out), .in_1(multiplexer_44_out), .out(R[3]));
  Multiplexer multiplexer_53 (.sel(B[3]), .in_0(multiplexer_37_out), .in_1(multiplexer_45_out), .out(R[4]));
  Multiplexer multiplexer_54 (.sel(B[3]), .in_0(multiplexer_38_out), .in_1(multiplexer_46_out), .out(R[5]));
  Multiplexer multiplexer_55 (.sel(B[3]), .in_0(multiplexer_39_out), .in_1(multiplexer_47_out), .out(R[6]));
  Multiplexer multiplexer_56 (.sel(B[3]), .in_0(multiplexer_40_out), .in_1(multiplexer_48_out), .out(R[7]));
  Multiplexer multiplexer_57 (.sel(B[3]), .in_0(multiplexer_41_out), .in_1(1'b0), .out(R[8]));
  Multiplexer multiplexer_58 (.sel(B[3]), .in_0(multiplexer_42_out), .in_1(1'b0), .out(R[9]));
  Multiplexer multiplexer_59 (.sel(B[3]), .in_0(multiplexer_43_out), .in_1(1'b0), .out(R[10]));
  Multiplexer multiplexer_60 (.sel(B[3]), .in_0(multiplexer_44_out), .in_1(1'b0), .out(R[11]));
  Multiplexer multiplexer_61 (.sel(B[3]), .in_0(multiplexer_45_out), .in_1(1'b0), .out(R[12]));
  Multiplexer multiplexer_62 (.sel(B[3]), .in_0(multiplexer_46_out), .in_1(1'b0), .out(R[13]));
  Multiplexer multiplexer_63 (.sel(B[3]), .in_0(multiplexer_47_out), .in_1(1'b0), .out(R[14]));
  Multiplexer multiplexer_64 (.sel(B[3]), .in_0(multiplexer_48_out), .in_1(1'b0), .out(R[15]));
endmodule
