// Digital circuit Zero_Output.dig as structural Verilog
module Zero_Output (
  input  [15:0] R,
  output Zero
);

  nor nor_1 (Zero, R[0], R[1], R[2], R[3], R[4], R[5], R[6], R[7], R[8], R[9], R[10], R[11], R[12], R[13], R[14], R[15]);
endmodule
